# Fritzing sketch GoXLR Clone (saved by Fritzing 1.0.1rc)
breadboards: 1

parts:
  Part1 = Arduino Nano (Rev3.0)
  R1 = Rotary Potentiometer (Small) [maximum_resistance=10kΩ knob_status=50% power=0.5W package=THT]
  R2 = Rotary Potentiometer (Small) [maximum_resistance=10kΩ knob_status=50% power=0.5W package=THT]
  R3 = Rotary Potentiometer (Small) [maximum_resistance=10kΩ knob_status=50% power=0.5W package=THT]
  S1 = Momentary Switch [package=ksa_sealed_tac_switch]

nets:
  N1: Part1.GND, R2.leg2, R3.leg2, S1.2
  N2: Part1.D2, S1.4
  N3: Part1.5V, R1.leg1, R2.leg1, R3.leg1
  N4: Part1.A2, R3.wiper
  N5: Part1.A1, R2.wiper
  N6: Part1.A0, R1.wiper

// code stored in the sketch: Arduino Code.ino
const int POTS = 3;
const int DELAY = 100;


int potPids[] = {A2, A1, A0};
int potVals[] = {0, 0, 0};


void setup() {
  Serial.begin(9600);
  Serial.print("Started\n");
}


void loop() {
  for (int i = 0; i < POTS; i++) {
    potVals[i] = analogRead(potPids[i]);
    float percentage = (float) potVals[i] / 1023 * 100;
    int roundedPercentage = (int) floor(percentage);
    Serial.print("pot");
    Serial.print(i);
    Serial.print("=");
    //Serial.print(roundedPercentage);
    //Serial.println("%");
    Serial.println(potVals[i]);
  }


  delay(DELAY);
}
